// Digital circuit ALU.dig as structural Verilog
module ALU (
  input  [31:0] A,
  input  [31:0] B,
  input  [31:0] Data,
  input  Enable,
  input  [3:0] Instruction,
  input  CarryIn,
  output [31:0] REGA,
  output [31:0] REGB,
  output Carry
);

  wire add_1_c_o, Carry_t, not_1_out, sub_1_c_o;
  wire [31:0] add_1_s, B_t, div_1_q, div_1_r, multiplexer_4_out, REGA_t, REGB_t, sub_1_s;
  wire [63:0] mul_1_mul;

  Multiplexer #(.Bits(32), .generic("this.Bits = args.bits;")) multiplexer_1 (
    .sel(Enable), .in_0(A), .in_1(REGA_t), .out(REGA));
  Multiplexer #(.Bits(32), .generic("this.Bits = args.bits;")) multiplexer_2 (
    .sel(Enable), .in_0(B), .in_1(REGB_t), .out(REGB));
  Multiplexer multiplexer_3 (.sel(Enable), .in_0(CarryIn), .in_1(Carry_t), .out(Carry));
  Add #(.Bits(32), .generic("this.Bits = args.bits;")) add_1 (
    .a(A), .b(B_t), .c_i(CarryIn), .s(add_1_s), .c_o(add_1_c_o));
  Sub #(.Bits(32), .generic("this.Bits = args.bits;")) sub_1 (
    .a(A), .b(B_t), .c_i(CarryIn), .s(sub_1_s), .c_o(sub_1_c_o));
  Mul #(.Bits(32), .generic("this.Bits = args.bits;")) mul_1 (.a(A), .b(B_t), .mul(mul_1_mul));
  Div #(.Bits(32), .generic("this.Bits = args.bits;")) div_1 (.a(A), .b(B_t), .q(div_1_q), .r(div_1_r));
  Multiplexer #(.Bits(32), .generic("this.Bits = args.bits;")) multiplexer_4 (
    .sel(not_1_out), .in_0(mul_1_mul[63:32]), .in_1(B), .out(multiplexer_4_out));
  not not_1 (not_1_out, Instruction[3]);
  Multiplexer #(.Selector_Bits(3), .Bits(32), .generic("this.Bits = args.bits;")) multiplexer_5 (
    .sel(Instruction[2:0]), .in_0(mul_1_mul[31:0]), .in_1(add_1_s), .in_2(sub_1_s), .in_3(mul_1_mul[31:0]),
    .in_4(div_1_q), .in_5(div_1_r), .in_6(div_1_q), .in_7(mul_1_mul[31:0]), .out(REGA_t));
  Multiplexer #(.Selector_Bits(3), .Bits(32), .generic("this.Bits = args.bits;")) multiplexer_6 (
    .sel(Instruction[2:0]), .in_0(multiplexer_4_out), .in_1(B), .in_2(B), .in_3(B), .in_4(B), .in_5(B),
    .in_6(div_1_r), .in_7(mul_1_mul[63:32]), .out(REGB_t));
  Multiplexer #(.Bits(32), .generic("this.Bits = args.bits;")) multiplexer_7 (
    .sel(Instruction[3]), .in_0(B), .in_1(Data), .out(B_t));
  Multiplexer #(.Selector_Bits(3)) multiplexer_8 (
    .sel(Instruction[2:0]), .in_0(CarryIn), .in_1(add_1_c_o), .in_2(sub_1_c_o), .in_3(CarryIn),
    .in_4(CarryIn), .in_5(CarryIn), .in_6(CarryIn), .in_7(CarryIn), .out(Carry_t));

  // Other names for the same wires on the sheet: Operation[2:0] = Instruction[2:0]; AFlag = Instruction[3];
  //   TrueB[31:0] = B
endmodule

/* Code that sets the parameters or builds the circuit:
bits := 24;
*/
