// Digital circuit Computer.dig as structural Verilog
module Computer (
  input  clk,
  input  LDCTR,
  input  [23:0] JMPDST
);

  wire ADD, CLK_t, comparator_1_eq, decoder_1_out_4, demultiplexer_1_out_0, demultiplexer_1_out_1,
       demultiplexer_1_out_2, DIV, DIVR, driverinvsel_1_out, HLT, JMP, JNZ, LDA, LDB, LDC, LDCTR_t, LDD,
       LDREGA, LDREGB, LDREGC, LDREGD, MUL, not_1_out, not_2_out, pulldown_1_out, reset_1_out, SUB, SWP;
  wire [7:0] Instruction;
  wire [23:0] A, add_1_s, B, C, CTR, D, Data, div_1_q, div_1_r, JMPDST_t, REGA, REGB, REGC, REGD, sub_1_s;
  wire [47:0] mul_1_mul;

  PullDown pulldown_1 (.out(pulldown_1_out));
  assign driverinvsel_1_out = ~HLT ? clk : 1'bz;  // DriverInvSel driverinvsel_1
  or or_1 (CLK_t, driverinvsel_1_out, 1'b0);
  Reset reset_1 (.out(reset_1_out));
  not not_1 (not_1_out, reset_1_out);
  Break break_1 (.brk(HLT));
  CounterPreset #(.maxValue(4194304), .Bits(24), .isProgramCounter("true")) Program_Counter (
    .en(1'b1), .C(CLK_t), .dir(pulldown_1_out), .in(JMPDST_t), .ld(LDCTR_t), .clr(not_1_out), .out(CTR));  // open: ovf
  ROM #(.bigEndian("true"), .AddrBits(24), .isProgramMemory("true"), .Bits(32)) rom_1 (
    .A(CTR), .sel(1'b1), .D({Data, Instruction}));
  or or_2 (LDCTR_t, JMP, LDCTR);
  PullDown pulldown_2 (.out(JMP));
  assign JMPDST_t = JMPDST | Data;  // Or or_3, 24 bits wide
  // Probe on CTR
  // Probe on A
  // Probe on B
  // Probe on C
  // Probe on D
  // Probe on Instruction
  // Probe on Data
  Register #(.Bits(24)) u_A (.D(REGA), .C(CLK_t), .en(LDREGA), .Q(A));
  PullDown pulldown_3 (.out(LDREGA));
  Register #(.Bits(24)) u_B (.D(REGB), .C(CLK_t), .en(LDREGB), .Q(B));
  PullDown pulldown_4 (.out(LDREGB));
  Register #(.Bits(24)) u_C (.D(REGC), .C(CLK_t), .en(LDREGC), .Q(C));
  PullDown pulldown_5 (.out(LDREGC));
  Register #(.Bits(24)) u_D (.D(REGD), .C(CLK_t), .en(LDREGD), .Q(D));
  PullDown pulldown_6 (.out(LDREGD));
  Add #(.Bits(24)) add_1 (.a(A), .b(Data), .c_i(1'b0), .s(add_1_s));  // open: c_o
  Sub #(.Bits(24)) sub_1 (.a(A), .b(Data), .c_i(1'b0), .s(sub_1_s));  // open: c_o
  Mul #(.Bits(24)) mul_1 (.a(A), .b(Data), .mul(mul_1_mul));
  Div #(.Bits(24)) div_1 (.a(A), .b(Data), .q(div_1_q), .r(div_1_r));
  assign REGA = ADD ? add_1_s : 24'bz;  // Driver driver_1
  assign REGA = SUB ? sub_1_s : 24'bz;  // Driver driver_2
  assign REGA = MUL ? mul_1_mul[23:0] : 24'bz;  // Driver driver_3
  assign REGA = DIV ? div_1_q : 24'bz;  // Driver driver_4
  assign REGB = DIVR ? div_1_r : 24'bz;  // Driver driver_5
  Decoder #(.Selector_Bits(8)) decoder_1 (
    .sel(Instruction), .out_0(LDA), .out_1(LDB), .out_2(LDC), .out_3(LDD), .out_4(decoder_1_out_4),
    .out_5(JNZ), .out_6(ADD), .out_7(SUB), .out_8(MUL), .out_9(DIV), .out_10(DIVR), .out_11(SWP),
    .out_255(HLT));  // open: out_12, out_13, out_14, out_15, out_16, out_17, out_18, out_19, out_20, out_21, out_22, out_23, out_24, out_25, out_26, out_27, out_28, out_29, out_30, out_31, out_32, out_33, out_34, out_35, out_36, out_37, out_38, out_39, out_40, out_41, out_42, out_43, out_44, out_45, out_46, out_47, out_48, out_49, out_50, out_51, out_52, out_53, out_54, out_55, out_56, out_57, out_58, out_59, out_60, out_61, out_62, out_63, out_64, out_65, out_66, out_67, out_68, out_69, out_70, out_71, out_72, out_73, out_74, out_75, out_76, out_77, out_78, out_79, out_80, out_81, out_82, out_83, out_84, out_85, out_86, out_87, out_88, out_89, out_90, out_91, out_92, out_93, out_94, out_95, out_96, out_97, out_98, out_99, out_100, out_101, out_102, out_103, out_104, out_105, out_106, out_107, out_108, out_109, out_110, out_111, out_112, out_113, out_114, out_115, out_116, out_117, out_118, out_119, out_120, out_121, out_122, out_123, out_124, out_125, out_126, out_127, out_128, out_129, out_130, out_131, out_132, out_133, out_134, out_135, out_136, out_137, out_138, out_139, out_140, out_141, out_142, out_143, out_144, out_145, out_146, out_147, out_148, out_149, out_150, out_151, out_152, out_153, out_154, out_155, out_156, out_157, out_158, out_159, out_160, out_161, out_162, out_163, out_164, out_165, out_166, out_167, out_168, out_169, out_170, out_171, out_172, out_173, out_174, out_175, out_176, out_177, out_178, out_179, out_180, out_181, out_182, out_183, out_184, out_185, out_186, out_187, out_188, out_189, out_190, out_191, out_192, out_193, out_194, out_195, out_196, out_197, out_198, out_199, out_200, out_201, out_202, out_203, out_204, out_205, out_206, out_207, out_208, out_209, out_210, out_211, out_212, out_213, out_214, out_215, out_216, out_217, out_218, out_219, out_220, out_221, out_222, out_223, out_224, out_225, out_226, out_227, out_228, out_229, out_230, out_231, out_232, out_233, out_234, out_235, out_236, out_237, out_238, out_239, out_240, out_241, out_242, out_243, out_244, out_245, out_246, out_247, out_248, out_249, out_250, out_251, out_252, out_253, out_254
  Diode diode_1 (.I(decoder_1_out_4), .O(JMP));
  Diode diode_2 (.I(ADD), .O(LDREGA));
  Diode diode_3 (.I(SUB), .O(LDREGA));
  Diode diode_4 (.I(MUL), .O(LDREGA));
  Diode diode_5 (.I(MUL), .O(LDREGA));
  Diode diode_6 (.I(DIV), .O(LDREGA));
  Diode diode_7 (.I(DIVR), .O(LDREGA));
  Diode diode_8 (.I(DIVR), .O(LDREGB));
  Diode diode_9 (.I(LDA), .O(LDREGA));
  assign REGA = LDA ? Data : 24'bz;  // Driver driver_6
  Diode diode_10 (.I(LDC), .O(LDREGC));
  assign REGC = LDC ? Data : 24'bz;  // Driver driver_7
  Diode diode_11 (.I(SWP), .O(LDREGA));
  Comparator #(.Bits(24)) comparator_1 (.a(A), .b({24{1'b0}}), .eq(comparator_1_eq));  // open: gt, lt
  Demultiplexer #(.Selector_Bits(2)) demultiplexer_1 (
    .sel(Data[1:0]), .in(SWP), .out_0(demultiplexer_1_out_0), .out_1(demultiplexer_1_out_1),
    .out_2(demultiplexer_1_out_2));  // open: out_3
  not not_2 (not_2_out, comparator_1_eq);
  assign REGB = demultiplexer_1_out_0 ? A : 24'bz;  // Driver driver_8
  assign REGC = demultiplexer_1_out_1 ? A : 24'bz;  // Driver driver_9
  assign REGA = demultiplexer_1_out_0 ? B : 24'bz;  // Driver driver_10
  assign JMP = JNZ ? not_2_out : 1'bz;  // Driver driver_11
  assign REGD = demultiplexer_1_out_2 ? A : 24'bz;  // Driver driver_12
  Diode diode_12 (.I(demultiplexer_1_out_0), .O(LDREGB));
  Diode diode_13 (.I(demultiplexer_1_out_1), .O(LDREGC));
  Diode diode_14 (.I(demultiplexer_1_out_2), .O(LDREGD));
  assign REGA = demultiplexer_1_out_1 ? C : 24'bz;  // Driver driver_13
  assign REGA = demultiplexer_1_out_2 ? D : 24'bz;  // Driver driver_14
  Diode diode_15 (.I(LDB), .O(LDREGB));
  assign REGB = LDB ? Data : 24'bz;  // Driver driver_15
  Diode diode_16 (.I(LDD), .O(LDREGD));
  assign REGD = LDD ? Data : 24'bz;  // Driver driver_16

  // Notes on the sheet:
  //   clk: Hz: 100
  //   Read ROM
  //   contents of rom_1 (hex, n*v repeats v):
  //   ffffff01,ff02,ff0003,ff000000,604,ff,705,f000000a,ff000706,30a
  //   ,10*0,504
endmodule
