// Digital circuit JMP.dig as structural Verilog
module JMP (
  input  [31:0] A,
  input  [31:0] B,
  input  [31:0] Data,
  input  Enable,
  input  [3:0] Instruction,
  input  Carry,
  output [31:0] Counter,
  output JMP
);

  wire comparator_1_eq, comparator_1_gt, comparator_1_lt, comparator_2_eq, multiplexer_1_out, not_1_out,
       not_2_out, not_3_out, or_1_out, or_2_out;

  Comparator #(.Bits(32), .generic("this.Bits = args.bits;")) comparator_1 (
    .a(A), .b(B), .gt(comparator_1_gt), .eq(comparator_1_eq), .lt(comparator_1_lt));
  Comparator #(.Bits(32), .generic("this.Bits = args.bits;")) comparator_2 (
    .a(A), .b({32{1'b0}}), .eq(comparator_2_eq));  // open: gt, lt
  or or_1 (or_1_out, comparator_1_gt, comparator_1_eq);
  or or_2 (or_2_out, comparator_1_eq, comparator_1_lt);
  not not_1 (not_1_out, comparator_2_eq);
  not not_2 (not_2_out, comparator_1_eq);
  not not_3 (not_3_out, Carry);
  Multiplexer #(.Selector_Bits(4)) multiplexer_1 (
    .sel(Instruction), .in_0(1'b1), .in_1(comparator_2_eq), .in_2(not_1_out), .in_3(comparator_1_gt),
    .in_4(or_1_out), .in_5(comparator_1_lt), .in_6(or_2_out), .in_7(comparator_1_eq), .in_8(not_2_out),
    .in_9(Carry), .in_10(not_3_out), .in_11(1'b0), .in_12(1'b0), .in_13(1'b0), .in_14(1'b0), .in_15(1'b0),
    .out(multiplexer_1_out));
  and and_1 (JMP, multiplexer_1_out, Enable);

  assign Counter = Data;
endmodule

/* Code that sets the parameters or builds the circuit:
bits := 24;
*/
