// Digital circuit LD.dig as structural Verilog
module LD (
  input  [31:0] A,
  input  [31:0] B,
  input  [31:0] C,
  input  [31:0] D,
  input  [31:0] Data,
  input  Enable,
  input  [3:0] Instruction,
  output [31:0] REGA,
  output [31:0] REGB,
  output [31:0] REGC,
  output [31:0] REGD
);

  wire demultiplexer_1_out_0, demultiplexer_1_out_1, demultiplexer_1_out_2, demultiplexer_1_out_3,
       demultiplexer_1_out_4, demultiplexer_1_out_5;
  wire [31:0] multiplexer_1_out, multiplexer_2_out, multiplexer_3_out, multiplexer_4_out, mv_1_rega,
       mv_1_regb, mv_1_regc, mv_1_regd;

  Multiplexer #(.Bits(32), .generic("this.Bits = args.bits;")) multiplexer_1 (
    .sel(demultiplexer_1_out_0), .in_0(A), .in_1(Data), .out(multiplexer_1_out));
  Multiplexer #(.Bits(32), .generic("this.Bits = args.bits;")) multiplexer_2 (
    .sel(demultiplexer_1_out_1), .in_0(B), .in_1(Data), .out(multiplexer_2_out));
  Multiplexer #(.Bits(32), .generic("this.Bits = args.bits;")) multiplexer_3 (
    .sel(demultiplexer_1_out_2), .in_0(C), .in_1(Data), .out(multiplexer_3_out));
  Multiplexer #(.Bits(32), .generic("this.Bits = args.bits;")) multiplexer_4 (
    .sel(demultiplexer_1_out_3), .in_0(D), .in_1(Data), .out(multiplexer_4_out));
  Demultiplexer #(.Selector_Bits(4)) demultiplexer_1 (
    .sel(Instruction), .in(Enable), .out_0(demultiplexer_1_out_0), .out_1(demultiplexer_1_out_1),
    .out_2(demultiplexer_1_out_2), .out_3(demultiplexer_1_out_3), .out_4(demultiplexer_1_out_4),
    .out_5(demultiplexer_1_out_5));  // open: out_6, out_7, out_8, out_9, out_10, out_11, out_12, out_13, out_14, out_15
  MV #(.generic("bits := args.bits;")) mv_1 (
    .A(multiplexer_1_out), .B(multiplexer_2_out), .C(multiplexer_3_out), .D(multiplexer_4_out), .Data(Data),
    .Enable(demultiplexer_1_out_4), .REGA(mv_1_rega), .REGB(mv_1_regb), .REGC(mv_1_regc), .REGD(mv_1_regd));
  SWP #(.generic("bits := args.bits;")) swp_1 (
    .A(mv_1_rega), .B(mv_1_regb), .C(mv_1_regc), .D(mv_1_regd), .Data(Data), .Enable(demultiplexer_1_out_5),
    .REGA(REGA), .REGB(REGB), .REGC(REGC), .REGD(REGD));
endmodule

/* Code that sets the parameters or builds the circuit:
bits := 24;
*/
