// Digital circuit MV.dig as structural Verilog
module MV (
  input  [31:0] A,
  input  [31:0] B,
  input  [31:0] C,
  input  [31:0] D,
  input  [31:0] Data,
  input  Enable,
  output [31:0] REGA,
  output [31:0] REGB,
  output [31:0] REGC,
  output [31:0] REGD
);

  wire not_1_out, not_2_out, not_3_out, not_4_out;
  wire [31:0] driver_1_out, driver_2_out;

  assign driver_1_out = Enable ? Data : 32'bz;  // Driver driver_1
  PullDown #(.Bits(32), .generic("this.Bits = args.bits;")) pulldown_1 (.out(driver_1_out));
  not not_1 (not_1_out, driver_1_out[4]);
  not not_2 (not_2_out, driver_1_out[5]);
  not not_3 (not_3_out, driver_1_out[6]);
  not not_4 (not_4_out, driver_1_out[7]);
  assign driver_2_out = driver_1_out[0] ? A : 32'bz;  // Driver driver_2
  assign driver_2_out = driver_1_out[1] ? B : 32'bz;  // Driver driver_3
  assign driver_2_out = driver_1_out[2] ? C : 32'bz;  // Driver driver_4
  assign driver_2_out = driver_1_out[3] ? D : 32'bz;  // Driver driver_5
  Multiplexer #(.Bits(32), .generic("this.Bits = args.bits;")) multiplexer_1 (
    .sel(not_1_out), .in_0(driver_2_out), .in_1(A), .out(REGA));
  Multiplexer #(.Bits(32), .generic("this.Bits = args.bits;")) multiplexer_2 (
    .sel(not_2_out), .in_0(driver_2_out), .in_1(B), .out(REGB));
  Multiplexer #(.Bits(32), .generic("this.Bits = args.bits;")) multiplexer_3 (
    .sel(not_3_out), .in_0(driver_2_out), .in_1(C), .out(REGC));
  Multiplexer #(.Bits(32), .generic("this.Bits = args.bits;")) multiplexer_4 (
    .sel(not_4_out), .in_0(driver_2_out), .in_1(D), .out(REGD));
endmodule

/* Code that sets the parameters or builds the circuit:
bits := 24;
*/
