// Digital circuit Stack.dig as structural Verilog
module Stack (
  input  [23:0] A,
  input  [3:0] Instruction,
  input  Enable,
  input  [23:0] Data,
  output [23:0] RegA
);

  wire add_1_s, and_1_out, delay_1_out, demultiplexer_1_out_0, demultiplexer_1_out_1, demultiplexer_1_out_2,
       demultiplexer_1_out_3, demultiplexer_1_out_4, demultiplexer_1_out_5, multiplexer_1_out,
       multiplexer_2_out, multiplexer_4_out, or_1_out, or_2_out, ramdualport_1_d;
  wire [1:0] counterpreset_1_out;

  Multiplexer #(.generic("this.Bits = args.bits;")) multiplexer_1 (
    .sel(demultiplexer_1_out_0), .in_0(Data), .in_1(A), .out(multiplexer_1_out));
  Demultiplexer #(.Selector_Bits(4)) demultiplexer_1 (
    .sel(Instruction), .in(Enable), .out_0(demultiplexer_1_out_0), .out_1(demultiplexer_1_out_1),
    .out_2(demultiplexer_1_out_2), .out_3(demultiplexer_1_out_3), .out_4(demultiplexer_1_out_4),
    .out_5(demultiplexer_1_out_5));  // open: out_6, out_7, out_8, out_9, out_10, out_11, out_12, out_13, out_14, out_15
  Multiplexer #(.generic("this.Bits=args.bits;")) multiplexer_2 (
    .sel(demultiplexer_1_out_4), .in_0(A), .in_1(Data), .out(multiplexer_2_out));
  or or_1 (or_1_out, demultiplexer_1_out_0, demultiplexer_1_out_1, demultiplexer_1_out_2);
  RAMDualPort #(.generic("this.Bits = args.bits; this.AddrBits = args.bits;")) ramdualport_1 (
    .A(counterpreset_1_out), .Din(multiplexer_1_out), .str(or_1_out), .C(or_1_out),
    .ld(demultiplexer_1_out_2), .D(ramdualport_1_d));
  or or_2 (or_2_out, demultiplexer_1_out_0, demultiplexer_1_out_1);
  Multiplexer #(.generic("this.Bits = args.bits;")) multiplexer_3 (
    .sel(demultiplexer_1_out_2), .in_0(A), .in_1(ramdualport_1_d), .out(RegA));
  Multiplexer #(.generic("this.Bits=args.bits;")) multiplexer_4 (
    .sel(demultiplexer_1_out_5), .in_0(A), .in_1(add_1_s), .out(multiplexer_4_out));
  Add #(.generic("this.Bits=args.bits;")) add_1 (
    .a(multiplexer_2_out), .b(counterpreset_1_out), .c_i(1'b0), .s(add_1_s));  // open: c_o
  and and_1 (and_1_out, Enable, ~demultiplexer_1_out_3);  // And
  CounterPreset #(.generic("this.Bits=args.bits;")) counterpreset_1 (
    .en(Enable), .C(delay_1_out), .dir(~or_2_out), .in(multiplexer_4_out), .ld(demultiplexer_1_out_3),
    .clr(1'b0), .out(counterpreset_1_out));  // open: ovf
  Delay delay_1 (.in(and_1_out), .out(delay_1_out));
endmodule

/* Code that sets the parameters or builds the circuit:
bits := 8;
*/
