// Logisim project computer.circ as structural Verilog: 1 circuit, main circuit main
module main (
);

  wire and_1_out, button_1_out, clock_1_out, clock_2_out, decoder_1_out0, decoder_1_out1, decoder_1_out2,
       decoder_1_out3, HLT, LDCounter, nor_1_out, not_1_out, or_1_out;
  wire [7:0] Instruction;
  wire [23:0] Counter, CounterDST, Data, REGA, REGB, REGC, REGD;

  Clock clock_1 (.out(clock_1_out));
  and and_1 (and_1_out, not_1_out, or_1_out);
  or or_1 (or_1_out, clock_1_out, HLT);
  Button button_1 (.out(button_1_out));
  // NOT_Gate not_1 has open pins: in=open, out=not_1_out
  Counter #(.max('hffffff), .width(24)) ProgramCounter (
    .clr(button_1_out), .load(LDCounter), .clk(and_1_out), .D(CounterDST), .Q(Counter));  // open: up, count, carry
  ROM #(.addrWidth(24), .dataWidth(32)) InstructionMEM (.addr(Counter), .data({Data, Instruction}));
  Clock clock_2 (.out(clock_2_out));
  nor nor_1 (nor_1_out, Instruction[2], Instruction[3], Instruction[4], Instruction[5], Instruction[6], Instruction[7]);
  and and_2 (HLT, Instruction[0], Instruction[1], Instruction[2], Instruction[3], Instruction[4], Instruction[5], Instruction[6], Instruction[7]);
  Decoder #(.select(2)) decoder_1 (
    .out0(decoder_1_out0), .out1(decoder_1_out1), .out2(decoder_1_out2), .out3(decoder_1_out3),
    .sel(Instruction[1:0]), .en(nor_1_out));
  Register #(.width(24)) A (.D(Data), .en(decoder_1_out0), .clk(clock_2_out), .Q(REGA));  // open: clr
  Register #(.width(24)) B (.D(Data), .en(decoder_1_out1), .clk(clock_2_out), .Q(REGB));  // open: clr
  Register #(.width(24)) C (.D(Data), .en(decoder_1_out2), .clk(clock_2_out), .Q(REGC));  // open: clr
  Register #(.width(24)) D (.D(Data), .en(decoder_1_out3), .clk(clock_2_out), .Q(REGD));  // open: clr

  // Notes on the sheet:
  //   contents of InstructionMEM (hex, n*v repeats v):
  //   10000000 11111111 11111111 11111111 1000000 0 0 11111111 11000000 0 11111111 0 0 11111111
endmodule
